// Logisim project problem1.circ as structural Verilog
module main (
  input  in_1,
  input  in_2,
  output out_3,
  output out_4
);

  problem1 problem1_1 (.s(in_1), .r(in_2), .q(out_3), .qbar(out_4));
endmodule

// VHDL entity problem1, as the project stores it:
library ieee;
use ieee.std_logic_1164.all;

entity problem1 is
    port (
        s, r : in std_logic;
        q, qbar : out std_logic
    );
end problem1;

architecture structural of problem1 is
    signal qi, qbi : std_logic;
begin
    qi <= not (r or qbi);
    qbi <= not (s or qi);
    q <= qi;
    qbar <= qbi;
end structural;
