// Logisim project problem1_gates.circ as structural Verilog: 1 circuit, main circuit main
module main (
  input  s,
  input  r,
  output q,
  output qbar
);

  nor nor_1 (q, r, qbar);
  nor nor_2 (qbar, q, s);

  // Notes on the sheet:
  //   Problem 1. RS Latch
  //   All pins: 1 bit. Matching tunnel labels are electrically connected.
  //   Inputs above are operated with the Poke Tool. Apply initialization before testing Hold.
  //   Cross-coupled NOR gates
  //   s=r=1: q=qbar=0 (forbidden). Recover through Reset or Set.
endmodule
