// Logisim project problem2.circ as structural Verilog
module main (
  input  in_1,
  input  in_2,
  output out_3,
  output out_4
);

  problem2 problem2_1 (.d(in_1), .en(in_2), .q(out_3), .qbar(out_4));
endmodule

// VHDL entity problem2, as the project stores it:
library ieee;
use ieee.std_logic_1164.all;

entity problem2 is
    port (
        d, en : in std_logic;
        q, qbar : out std_logic
    );
end problem2;

architecture behavioral of problem2 is
    signal qi : std_logic;
begin
    process(d, en)
    begin
        if en = '1' then
            qi <= d;
        end if;
    end process;
    q <= qi;
    qbar <= not qi;
end behavioral;
