// Logisim project problem2_gates.circ as structural Verilog: 1 circuit, main circuit main
module main (
  input  d,
  input  en,
  output q,
  output qbar
);

  wire nD, nR, nS;

  nand nand_1 (nD, d, d);
  nand nand_2 (nS, d, en);
  nand nand_3 (nR, nD, en);
  nand nand_4 (q, nS, qbar);
  nand nand_5 (qbar, nR, q);

  // Notes on the sheet:
  //   Problem 2. D Latch
  //   All pins: 1 bit. Matching tunnel labels are electrically connected.
  //   Inputs above are operated with the Poke Tool. Apply initialization before testing Hold.
  //   NAND input gating
  //   Cross-coupled NAND latch
endmodule
