// Logisim project problem3.circ as structural Verilog
module main (
  input  in_1,
  input  in_2,
  output out_3,
  output out_4
);

  problem3 problem3_1 (.d(in_1), .clk(in_2), .q(out_3), .qbar(out_4));
endmodule

// VHDL entity problem3, as the project stores it:
library ieee;
use ieee.std_logic_1164.all;

entity problem3 is
    port (
        d, clk : in std_logic;
        q, qbar : out std_logic
    );
end problem3;

architecture behavioral of problem3 is
    signal qi : std_logic;
begin
    process(clk)
    begin
        if rising_edge(clk) then
            qi <= d;
        end if;
    end process;
    q <= qi;
    qbar <= not qi;
end behavioral;
