// Logisim project problem3_gates.circ as structural Verilog: 1 circuit, main circuit main
module main (
  input  d,
  input  clk,
  output q,
  output qbar
);

  wire MnD, MnR, MnS, Mq, Mqb, nclk, SnD, SnR, SnS;

  not not_1 (nclk, clk);
  nand nand_1 (MnD, d, d);
  nand nand_2 (MnS, d, nclk);
  nand nand_3 (MnR, MnD, nclk);
  nand nand_4 (Mq, MnS, Mqb);
  nand nand_5 (Mqb, MnR, Mq);
  nand nand_6 (SnD, Mq, Mq);
  nand nand_7 (SnS, Mq, clk);
  nand nand_8 (SnR, SnD, clk);
  nand nand_9 (q, SnS, qbar);
  nand nand_10 (qbar, SnR, q);

  // Notes on the sheet:
  //   Problem 3. D Flip-Flop
  //   All pins: 1 bit. Matching tunnel labels are electrically connected.
  //   Inputs above are operated with the Poke Tool. Apply initialization before testing Hold.
  //   Clock inversion
  //   MASTER (enable = nclk)
  //   SLAVE (enable = clk)
endmodule
