// Logisim project problem4.circ as structural Verilog
module main (
  input  in_1,
  input  in_2,
  input  in_3,
  output out_4,
  output out_5
);

  problem4 problem4_1 (.j(in_1), .k(in_2), .clk(in_3), .q(out_4), .qbar(out_5));
endmodule

// VHDL entity problem4, as the project stores it:
library ieee;
use ieee.std_logic_1164.all;

entity problem4 is
    port (
        j, k, clk : in std_logic;
        q, qbar : out std_logic
    );
end problem4;

architecture behavioral of problem4 is
    signal qi : std_logic;
begin
    process(clk)
    begin
        if rising_edge(clk) then
            if j = '0' and k = '0' then
                null;
            elsif j = '0' and k = '1' then
                qi <= '0';
            elsif j = '1' and k = '0' then
                qi <= '1';
            elsif j = '1' and k = '1' then
                qi <= not qi;
            end if;
        end if;
    end process;
    q <= qi;
    qbar <= not qi;
end behavioral;
