// Logisim project problem4_gates.circ as structural Verilog: 1 circuit, main circuit main
module main (
  input  j,
  input  k,
  input  clk,
  output q,
  output qbar
);

  wire D_jk, MnD, MnR, MnS, Mq, Mqb, n1, n2, nclk, nk, SnD, SnR, SnS;

  nand nand_1 (nk, k, k);
  nand nand_2 (nclk, clk, clk);
  nand nand_3 (MnD, D_jk, D_jk);
  nand nand_4 (MnS, D_jk, nclk);
  nand nand_5 (MnR, MnD, nclk);
  nand nand_6 (n1, j, qbar);
  nand nand_7 (Mq, MnS, Mqb);
  nand nand_8 (Mqb, MnR, Mq);
  nand nand_9 (n2, nk, q);
  nand nand_10 (SnD, Mq, Mq);
  nand nand_11 (SnS, Mq, clk);
  nand nand_12 (SnR, SnD, clk);
  nand nand_13 (D_jk, n1, n2);
  nand nand_14 (q, SnS, qbar);
  nand nand_15 (qbar, SnR, q);

  // Notes on the sheet:
  //   Problem 4. JK Flip-Flop
  //   All pins: 1 bit. Matching tunnel labels are electrically connected.
  //   Inputs above are operated with the Poke Tool. Apply initialization before testing Hold.
  //   NAND feedback logic: D_jk = (j AND qbar) OR ((NOT k) AND q)
  //   MASTER (enable = nclk)
  //   Feedback comes from the final SLAVE outputs q and qbar.
  //   SLAVE (enable = clk)
endmodule
