// Logisim project problem5.circ as structural Verilog
module main (
  input  in_1,
  input  in_2,
  input  in_3,
  input  in_4,
  output out_5,
  output out_6
);

  problem5 problem5_1 (.d(in_1), .clk(in_2), .set(in_3), .clr(in_4), .q(out_5), .qbar(out_6));
endmodule

// VHDL entity problem5, as the project stores it:
library ieee;
use ieee.std_logic_1164.all;

entity problem5 is
    port (
        d, clk, set, clr : in std_logic;
        q, qbar : out std_logic
    );
end problem5;

architecture behavioral of problem5 is
    signal qi : std_logic;
begin
    process(clk, set, clr)
    begin
        if clr = '1' then
            qi <= '0';
        elsif set = '1' then
            qi <= '1';
        elsif rising_edge(clk) then
            qi <= d;
        end if;
    end process;
    q <= qi;
    qbar <= not qi;
end behavioral;
