// Logisim project problem5_gates.circ as structural Verilog: 1 circuit, main circuit main
module main (
  input  d,
  input  clk,
  input  set,
  input  clr,
  output q,
  output qbar
);

  wire Em, Es, MnD, MnR, MnS, Mq, Mqb, Mrd, Msd, nclk, nclr, nset, S_eff, SnD, SnR, SnS, Srd, Ssd;

  not not_1 (nset, set);
  and and_1 (Em, nclk, nset, nclr);
  not not_2 (MnD, d);
  and and_2 (Msd, d, Em);
  and and_3 (Mrd, MnD, Em);
  not not_3 (SnD, Mq);
  and and_4 (Ssd, Mq, Es);
  and and_5 (Srd, SnD, Es);
  not not_4 (nclr, clr);
  nor nor_1 (MnS, S_eff, Msd);
  nor nor_2 (MnR, clr, Mrd);
  nor nor_3 (SnS, S_eff, Ssd);
  nor nor_4 (SnR, clr, Srd);
  not not_5 (nclk, clk);
  and and_6 (Es, clk, nset, nclr);
  nand nand_1 (Mq, MnS, Mqb);
  nand nand_2 (Mqb, MnR, Mq);
  nand nand_3 (q, SnS, qbar);
  nand nand_4 (qbar, SnR, q);
  and and_7 (S_eff, set, nclr);

  // Notes on the sheet:
  //   Problem 5. D Flip-Flop with Asynchronous Set and Clear
  //   All pins: 1 bit. Matching tunnel labels are electrically connected.
  //   Inputs above are operated with the Poke Tool. Apply initialization before testing Hold.
  //   Priority controls: S_eff = set AND NOT clr; clr overrides both latches.
  //   MASTER: gated data + asynchronous override
  //   SLAVE: gated data + asynchronous override
endmodule
